// Logisim project minh.circ as structural Verilog: 5 circuits, main circuit main
module main (
  input  [3:0] in_1,
  input  in_2,
  input  in_3,
  input  in_4,
  input  in_5,
  input  [3:0] in_6,
  input  in_7,
  input  in_8,
  input  in_9,
  input  in_10
);

  wire clock_1_out, n74192_2_pin4;
  wire [3:0] n74192_1_pin3, n74192_2_pin3;

  Clock clock_1 (.out(clock_1_out));
  _74192 u_74192_1 (
    .pin1(in_1[1]), .pin2(n74192_1_pin3[1]), .pin3(n74192_1_pin3[0]), .pin4(in_4), .pin5(clock_1_out),
    .pin6(n74192_1_pin3[2]), .pin7(n74192_1_pin3[3]), .pin15(in_1[0]), .pin14(in_2), .pin11(in_3),
    .pin10(in_1[2]), .pin9(in_1[3]));  // open: pin13, pin12
  _74192 u_74192_2 (
    .pin1(in_6[1]), .pin2(n74192_2_pin3[1]), .pin3(n74192_2_pin3[0]), .pin4(n74192_2_pin4), .pin5(in_9),
    .pin6(n74192_2_pin3[2]), .pin7(n74192_2_pin3[3]), .pin15(in_6[0]), .pin14(in_7), .pin11(in_8),
    .pin10(in_6[2]), .pin9(in_6[3]));  // open: pin13, pin12
  Clock clock_2 (.out(n74192_2_pin4));
  _7_Segment_Display u_7_segment_display_1 ();  // open: g, f, a, b, e, d, c, dp
  // BCD_to_7_Segment_decoder bcd_to_7_segment_decoder_1: pin names not known; wires that end beside it: 1'b1, 1'b0, n74192_1_pin3
  LED led_1 (.in(n74192_1_pin3[3]));
  LED led_2 (.in(n74192_1_pin3[2]));
  LED led_3 (.in(n74192_1_pin3[1]));
  LED led_4 (.in(n74192_1_pin3[0]));
  _7_Segment_Display u_7_segment_display_2 ();  // open: g, f, a, b, e, d, c, dp
  // BCD_to_7_Segment_decoder bcd_to_7_segment_decoder_2: pin names not known; wires that end beside it: 1'b1, 1'b0, n74192_2_pin3
  LED led_5 (.in(n74192_2_pin3[3]));
  LED led_6 (.in(n74192_2_pin3[2]));
  LED led_7 (.in(n74192_2_pin3[1]));
  LED led_8 (.in(n74192_2_pin3[0]));
  // Digital_Oscilloscope digital_oscilloscope_1: pin names not known; wires that end beside it: clock_1_out, n74192_1_pin3[0], n74192_1_pin3[1], n74192_1_pin3[2], n74192_1_pin3[3], in_5
  // Digital_Oscilloscope digital_oscilloscope_2: pin names not known; wires that end beside it: in_9, n74192_2_pin3[0], n74192_2_pin3[1], n74192_2_pin3[2], n74192_2_pin3[3], in_10
endmodule

module bai2 (
  input  [3:0] in_1,
  input  in_2,
  input  in_3,
  input  in_4,
  input  in_5,
  input  [3:0] in_6,
  input  in_7,
  input  in_8,
  input  in_9,
  input  in_10
);

  wire bcd_to_7_segment_decoder_2_p1, binary_to_bcd_converter_1_p3, binary_to_bcd_converter_2_p3,
       binary_to_bcd_converter_2_p5, clock_1_out, clock_2_out;
  wire [3:0] n74193_1_pin3, n74193_2_pin3;

  Clock clock_1 (.out(clock_1_out));
  Clock clock_2 (.out(clock_2_out));
  _74193 u_74193_1 (
    .pin1(in_1[1]), .pin2(n74193_1_pin3[1]), .pin3(n74193_1_pin3[0]), .pin4(in_4), .pin5(clock_1_out),
    .pin6(n74193_1_pin3[2]), .pin7(n74193_1_pin3[3]), .pin15(in_1[0]), .pin14(in_2), .pin11(in_3),
    .pin10(in_1[2]), .pin9(in_1[3]));  // open: pin13, pin12
  _74193 u_74193_2 (
    .pin1(in_6[1]), .pin2(n74193_2_pin3[1]), .pin3(n74193_2_pin3[0]), .pin4(clock_2_out), .pin5(in_9),
    .pin6(n74193_2_pin3[2]), .pin7(n74193_2_pin3[3]), .pin15(in_6[0]), .pin14(in_7), .pin11(in_8),
    .pin10(in_6[2]), .pin9(in_6[3]));  // open: pin13, pin12
  LED led_1 (.in(n74193_1_pin3[3]));
  _7_Segment_Display u_7_segment_display_1 ();  // open: g, f, a, b, e, d, c, dp
  _7_Segment_Display u_7_segment_display_2 ();  // open: g, f, a, b, e, d, c, dp
  // BCD_to_7_Segment_decoder bcd_to_7_segment_decoder_1: pin names not known
  // BCD_to_7_Segment_decoder bcd_to_7_segment_decoder_2: pin names not known; wires that end beside it: bcd_to_7_segment_decoder_2_p1
  // Binary_to_BCD_converter #(.binvalue(4)) binary_to_bcd_converter_1: pin names not known; wires that end beside it: 1'b0, n74193_1_pin3, binary_to_bcd_converter_1_p3, binary_to_bcd_converter_1_p3, bcd_to_7_segment_decoder_2_p1
  LED led_2 (.in(n74193_1_pin3[2]));
  LED led_3 (.in(n74193_1_pin3[1]));
  LED led_4 (.in(n74193_1_pin3[0]));
  _7_Segment_Display u_7_segment_display_3 ();  // open: g, f, a, b, e, d, c, dp
  // BCD_to_7_Segment_decoder bcd_to_7_segment_decoder_3: pin names not known
  // Binary_to_BCD_converter #(.binvalue(4)) binary_to_bcd_converter_2: pin names not known; wires that end beside it: 1'b0, n74193_2_pin3, binary_to_bcd_converter_2_p3, binary_to_bcd_converter_2_p3, binary_to_bcd_converter_2_p5
  LED led_5 (.in(n74193_2_pin3[3]));
  LED led_6 (.in(n74193_2_pin3[2]));
  LED led_7 (.in(n74193_2_pin3[1]));
  LED led_8 (.in(n74193_2_pin3[0]));
  // Digital_Oscilloscope digital_oscilloscope_1: pin names not known; wires that end beside it: clock_1_out, n74193_1_pin3[0], n74193_1_pin3[1], n74193_1_pin3[2], n74193_1_pin3[3], in_5
  _7_Segment_Display u_7_segment_display_4 ();  // open: g, f, a, b, e, d, c, dp
  // BCD_to_7_Segment_decoder bcd_to_7_segment_decoder_4: pin names not known; wires that end beside it: binary_to_bcd_converter_2_p5
  // Digital_Oscilloscope digital_oscilloscope_2: pin names not known; wires that end beside it: in_9, n74193_2_pin3[0], n74193_2_pin3[1], n74193_2_pin3[2], n74193_2_pin3[3], in_10
endmodule

module bai3 (
  input  in_1,
  input  in_2,
  input  [3:0] in_3,
  input  in_4
);

  wire clock_1_out, n7_segment_display_1_p1, n7_segment_display_2_p1, n74163_1_pin7;
  wire [3:0] n74163_1_pin14;

  Clock clock_1 (.out(clock_1_out));
  _74163 u_74163_1 (
    .pin1(in_2), .pin2(clock_1_out), .pin3(in_3[0]), .pin4(in_3[1]), .pin5(in_3[2]), .pin6(in_3[3]),
    .pin7(n74163_1_pin7), .pin14(n74163_1_pin14[0]), .pin13(n74163_1_pin14[1]), .pin12(n74163_1_pin14[2]),
    .pin11(n74163_1_pin14[3]), .pin10(n74163_1_pin7), .pin9(in_1));  // open: pin15
  // _7_Segment_Display 7_segment_display_1: pin names not known; wires that end beside it: n7_segment_display_1_p1, n7_segment_display_1_p1
  // BCD_to_7_Segment_decoder bcd_to_7_segment_decoder_1: pin names not known
  LED led_1 (.in(n74163_1_pin14[3]));
  LED led_2 (.in(n74163_1_pin14[2]));
  LED led_3 (.in(n74163_1_pin14[1]));
  // _7_Segment_Display 7_segment_display_2: pin names not known; wires that end beside it: n7_segment_display_2_p1, n7_segment_display_2_p1
  // BCD_to_7_Segment_decoder bcd_to_7_segment_decoder_2: pin names not known
  // Binary_to_BCD_converter #(.binvalue(4)) binary_to_bcd_converter_1: pin names not known; wires that end beside it: 1'b0, n74163_1_pin7, n74163_1_pin14
  LED led_4 (.in(n74163_1_pin14[0]));
  // Digital_Oscilloscope digital_oscilloscope_1: pin names not known; wires that end beside it: clock_1_out, n74163_1_pin14[0], n74163_1_pin14[1], n74163_1_pin14[2], n74163_1_pin14[3], in_4
  // also tied to VCC on the sheet: n74163_1_pin7
endmodule

module bai4 (
  input  in_1
);

  wire clock_1_out, n74164_1_pin3, n74164_1_pin4, n74164_1_pin5, n74164_1_pin6, n74164_1_pin10,
       n74164_1_pin11, n74164_1_pin12, n74164_1_pin13, not_1_out, not_2_out;

  Clock clock_1 (.out(clock_1_out));
  not not_1 (not_1_out, in_1);
  not not_2 (not_2_out, n74164_1_pin13);
  LED led_1 (.in(n74164_1_pin13));
  _74164 u_74164_1 (
    .pin1(not_2_out), .pin2(not_2_out), .pin3(n74164_1_pin3), .pin4(n74164_1_pin4), .pin5(n74164_1_pin5),
    .pin6(n74164_1_pin6), .pin13(n74164_1_pin13), .pin12(n74164_1_pin12), .pin11(n74164_1_pin11),
    .pin10(n74164_1_pin10), .pin9(in_1), .pin8(clock_1_out));
  LED led_2 (.in(n74164_1_pin12));
  LED led_3 (.in(n74164_1_pin11));
  LED led_4 (.in(n74164_1_pin10));
  LED led_5 (.in(n74164_1_pin6));
  LED led_6 (.in(n74164_1_pin5));
  LED led_7 (.in(n74164_1_pin4));
  LED led_8 (.in(n74164_1_pin3));
  // Digital_Oscilloscope digital_oscilloscope_1: pin names not known; wires that end beside it: 1'b0, clock_1_out, n74164_1_pin13, n74164_1_pin12, n74164_1_pin11, n74164_1_pin10, n74164_1_pin6, n74164_1_pin5, n74164_1_pin4, n74164_1_pin3, not_1_out
endmodule

module bai5 (
  input  [7:0] in_1,
  input  in_2,
  input  in_3,
  input  in_4
);

  wire clock_1_out, n74165_1_pin7, n74165_1_pin9;

  Clock clock_1 (.out(clock_1_out));
  _74165 u_74165_1 (
    .pin1(in_3), .pin2(clock_1_out), .pin3(in_1[4]), .pin4(in_1[5]), .pin5(in_1[6]), .pin6(in_1[7]),
    .pin7(n74165_1_pin7), .pin15(in_2), .pin14(in_1[3]), .pin13(in_1[2]), .pin12(in_1[1]), .pin11(in_1[0]),
    .pin10(n74165_1_pin7), .pin9(n74165_1_pin9));
  LED led_1 (.in(n74165_1_pin9));
  // Digital_Oscilloscope digital_oscilloscope_1: pin names not known; wires that end beside it: 1'b0, clock_1_out, n74165_1_pin9, n74165_1_pin7, in_4
endmodule
